# Fritzing sketch KITT (saved by Fritzing 0.6.3b)
breadboards: 1

parts:
  Arduino1 = Arduino
  J1 = Piezo Speaker
  R1 = Resistor [tolerance=±5% resistance=220 package=THT]
  R2 = Resistor [tolerance=±5% resistance=220 package=THT]
  R3 = Resistor [tolerance=±5% resistance=220 package=THT]
  LED1 = LED - 5mm [color="Red (633nm)" package="5 mm [THT]"]
  LED2 = LED - 5mm [color="Red (633nm)" package="5 mm [THT]"]
  LED3 = LED - 5mm [color="Red (633nm)" package="5 mm [THT]"]
  R4 = Trimmer Potentiometer [maximum_resistance=10kΩ package=THT]

nets:
  N1: Arduino1.GND, J1.pin1, LED1.cathode, LED2.cathode, LED3.cathode, R4.leg1
  N2: Arduino1.D9, J1.pin2
  N3: Arduino1.D5, R3.Pin_0
  N4: Arduino1.D4, R2.Pin_0
  N5: Arduino1.D3, R1.Pin_0
  N6: Arduino1.+5V, R4.leg2
  N7: Arduino1.A2, R4.wiper
  N8: R1.Pin_1, LED1.anode
  N9: R2.Pin_1, LED2.anode
  N10: R3.Pin_1, LED3.anode
